# Fritzing sketch circuit (saved by Fritzing 1.0.4)
breadboards: 1

parts:
  Raspberry_Pi_1 = Raspberry Pi 3 [part_number=RPI-3-V1.2]
  R1 = Resistor [tolerance=±5% resistance=1k package="2512 [SMD]"]
  U1 = ATTINY13 [package=dip]
  R3 = Resistor [tolerance=±5% resistance=1k package="2512 [SMD]"]
  R4 = Resistor [tolerance=±5% resistance=1k package="2512 [SMD]"]
  R5 = Resistor [tolerance=±5% resistance=1k package="2512 [SMD]"]
  LED1 = smd LED [color="Red (633nm)" package="0805 [SMD]"]
  R6 = Resistor [tolerance=±5% resistance=1k package="2512 [SMD]"]

nets:
  3V3: Raspberry_Pi_1.3v3, Raspberry_Pi_1.GPIO22, Raspberry_Pi_1.3V3, Raspberry_Pi_1.GPIO10, Raspberry_Pi_1.GPIO9, Raspberry_Pi_1.GPIO11
  N1: R1.Pin_0, U1.VCC, R3.Pin_0, R4.Pin_0, R5.Pin_0
  N2: R1.Pin_1, U1.PB5(NRES)
  N3: U1.PB3(ADC3), LED1.anode
  N4: U1.GND, R6.Pin_0
  N5: U1.PB0(MOSI), R3.Pin_1
  N6: U1.PB1(MISO), R4.Pin_1
  N7: U1.PB2(SCK_ADC1), R5.Pin_1
  N8: LED1.cathode, R6.Pin_1
